# Fritzing sketch schemat_2UV (saved by Fritzing 0.9.3b)

parts:
  Konwerter_stanów_logicznych_5V_-_3V3 = Logic Level Converter
  Wyświetlacz_LCD_-_2x16 = LCD-16X2 [package=lcd-16x2]
  Czytnik_microSD = MicroSD Card Module
  Kontaktron_(zamknięcie_osłony) = SWITCH-MOMENTARY-2 [package=reed_switch_plastic]
  Zasilanie_5V = Lilypad Battery Connect
  Źródło_prądowe_700mA = Lilypad Battery Connect
  U3 = Luxeon LED [package=luxeon]
  U4 = Luxeon LED [package=luxeon]
  U5 = Luxeon LED [package=luxeon]
  U6 = Luxeon LED [package=luxeon]
  U7 = Luxeon LED [package=luxeon]
  Konwerter_stanów_logicznych_5V_-_3V3_2 = Logic Level Converter
  Przycisk_chwilowy = Momentary Switch [package=ksa_sealed_tac_switch]
  R1 = Resistor [tolerance=±5% resistance=220 package=THT]
  Enkoder_obrotowy = Rotary Encoder [package=THT]
  R2 = Resistor [tolerance=±5% resistance=220 package=THT]
  R3 = Resistor [tolerance=±5% resistance=220 package=THT]
  Diody_UV = Luxeon LED [package=luxeon]
  USB_Power_1 = USB connector [package=THT]
  Sterownik_LCD = LCM1602 IIC [part_number="LCM1602 IIC" chip_label="LCM1602 IIC" package="DIP (Dual Inline) [THT]"]
  Przekaźnik_-_diody_UV = Keyes Relay [package=THT]
  Przekaźnik_-_podświetlenie_ekranu = Keyes Relay [package=THT]
  Raspberry_Pi_4 = Raspberry Pi 4 [part_number=RPI-4-b]
  Kamera_MIPI = TTL Serial JPEG Camera
  USB_Power_2 = USB connector [package=THT]
  Wyświetlacz_LCD_-_podświetlenie = 1.8" TFT Display with uSD
  Wyświetlacz_LCD_-_bez_podświetlenia = 1.8" TFT Display with uSD

nets:
  N1: Konwerter_stanów_logicznych_5V_-_3V3.TX2_LV, Raspberry_Pi_4.GPIO16
  N2: Konwerter_stanów_logicznych_5V_-_3V3.RX2_LV, Raspberry_Pi_4.GPIO20
  GND: Konwerter_stanów_logicznych_5V_-_3V3.GND, Czytnik_microSD.GND, Zasilanie_5V.-, Konwerter_stanów_logicznych_5V_-_3V3_2.GND, R3.Pin_1, USB_Power_1.GND, Sterownik_LCD.GND, Przekaźnik_-_diody_UV.ground, Przekaźnik_-_podświetlenie_ekranu.ground, Raspberry_Pi_4.GND, USB_Power_2.GND
  N3: Konwerter_stanów_logicznych_5V_-_3V3.LV, Kontaktron_(zamknięcie_osłony).1, Konwerter_stanów_logicznych_5V_-_3V3_2.LV, Przycisk_chwilowy.4, R2.Pin_1, Raspberry_Pi_4.3v3
  N4: Konwerter_stanów_logicznych_5V_-_3V3.RX_LV, Raspberry_Pi_4.GPIO3
  N5: Konwerter_stanów_logicznych_5V_-_3V3.TX_LV, Raspberry_Pi_4.GPIO2
  N6: Konwerter_stanów_logicznych_5V_-_3V3.TX_HV, Sterownik_LCD.SDA
  N7: Konwerter_stanów_logicznych_5V_-_3V3.RX_HV, Sterownik_LCD.SCL
  VCC: Konwerter_stanów_logicznych_5V_-_3V3.HV, Czytnik_microSD.VCC, Zasilanie_5V.+, Konwerter_stanów_logicznych_5V_-_3V3_2.HV, USB_Power_1.5V, Sterownik_LCD.VCC, Przekaźnik_-_diody_UV.power, Przekaźnik_-_podświetlenie_ekranu.power, USB_Power_2.5V, USB_Power_2.d+
  N8: Konwerter_stanów_logicznych_5V_-_3V3.RX2_HV, Przekaźnik_-_podświetlenie_ekranu.signal
  N9: Konwerter_stanów_logicznych_5V_-_3V3.TX2_HV, Przekaźnik_-_diody_UV.signal
  VSS: Wyświetlacz_LCD_-_2x16.VSS, Sterownik_LCD.VSS
  VDD: Wyświetlacz_LCD_-_2x16.VDD, Sterownik_LCD.VDD
  N10: Wyświetlacz_LCD_-_2x16.VO, Sterownik_LCD.V0
  N11: Wyświetlacz_LCD_-_2x16.RS, Sterownik_LCD.RS
  N12: Wyświetlacz_LCD_-_2x16.R_W, Sterownik_LCD.RW
  N13: Wyświetlacz_LCD_-_2x16.E, Sterownik_LCD.E
  N14: Wyświetlacz_LCD_-_2x16.DB0, Sterownik_LCD.D0
  N15: Wyświetlacz_LCD_-_2x16.DB1, Sterownik_LCD.D1
  N16: Wyświetlacz_LCD_-_2x16.DB2, Sterownik_LCD.D2
  N17: Wyświetlacz_LCD_-_2x16.DB3, Sterownik_LCD.D3
  N18: Wyświetlacz_LCD_-_2x16.DB4, Sterownik_LCD.D4
  N19: Wyświetlacz_LCD_-_2x16.DB5, Sterownik_LCD.D5
  N20: Wyświetlacz_LCD_-_2x16.DB6, Sterownik_LCD.D6
  N21: Wyświetlacz_LCD_-_2x16.DB7, Sterownik_LCD.D7
  N22: Wyświetlacz_LCD_-_2x16.A, Sterownik_LCD.A
  N23: Wyświetlacz_LCD_-_2x16.K, Sterownik_LCD.K
  N24: Czytnik_microSD.MISO, Konwerter_stanów_logicznych_5V_-_3V3_2.RX2_HV, Konwerter_stanów_logicznych_5V_-_3V3_2.TX2_HV
  N25: Czytnik_microSD.MOSI, Konwerter_stanów_logicznych_5V_-_3V3_2.RX_HV
  N26: Czytnik_microSD.SCK, Konwerter_stanów_logicznych_5V_-_3V3_2.TX_HV
  N27: Kontaktron_(zamknięcie_osłony).2, R3.Pin_0
  N28: Źródło_prądowe_700mA.-, U7.C
  N29: Źródło_prądowe_700mA.+, Przekaźnik_-_diody_UV.C
  N30: U3.A, Diody_UV.C
  N31: U3.C, U4.A
  N32: U4.C, U5.A
  N33: U5.C, U6.A
  N34: U6.C, U7.A
  N35: Konwerter_stanów_logicznych_5V_-_3V3_2.TX2_LV, Konwerter_stanów_logicznych_5V_-_3V3_2.RX2_LV, Raspberry_Pi_4.GPIO9
  N36: Konwerter_stanów_logicznych_5V_-_3V3_2.RX_LV, Raspberry_Pi_4.GPIO10
  N37: Konwerter_stanów_logicznych_5V_-_3V3_2.TX_LV, Raspberry_Pi_4.GPIO11
  N38: Przycisk_chwilowy.2, R1.Pin_0
  N39: R1.Pin_1, Raspberry_Pi_4.GPIO21
  N40: Enkoder_obrotowy.EncoderPinA, Raspberry_Pi_4.GPIO19
  N41: Enkoder_obrotowy.EncoderPinC, R2.Pin_0
  N42: Enkoder_obrotowy.EncoderPinB, Raspberry_Pi_4.GPIO26
  N43: Diody_UV.A, Przekaźnik_-_diody_UV.NO
  N44: USB_Power_1.USB, Raspberry_Pi_4.USB_Power
  N45: Przekaźnik_-_podświetlenie_ekranu.C, Wyświetlacz_LCD_-_bez_podświetlenia.VCC_backlight
  N46: Przekaźnik_-_podświetlenie_ekranu.NO, Wyświetlacz_LCD_-_podświetlenie.VCC_backlight
  N47: Raspberry_Pi_4.CSI, Kamera_MIPI.CSI
  N48: Raspberry_Pi_4.HDMI_0, Wyświetlacz_LCD_-_bez_podświetlenia.HDMI
  N49: USB_Power_2.USB, Wyświetlacz_LCD_-_bez_podświetlenia.USB_Power
  N50: Wyświetlacz_LCD_-_podświetlenie.GND_backlight_0, Wyświetlacz_LCD_-_bez_podświetlenia.GND_backlight_0
  N51: Wyświetlacz_LCD_-_podświetlenie.GND_backlight_1, Wyświetlacz_LCD_-_bez_podświetlenia.GND_backlight_1

custom parts:
  LCM1602 IIC: I2C-Module to use a 1602 or 2004 LCD on with the wire.h libory Serial LCD Modul
  Keyes Relay: The Keyes 5V relay module is suitable for SCM development, home appliance control. It uses a 5V~12V TIL control signal which can control DC / AC signal.
  Raspberry Pi 4: The RPi4, a faster version of the awesome Raspberry Pi 2 B ARM Board with 40 pin gpio. Ready for special Raspberry Pi B+ and RPi2 Hat (Hardware attached (on) top)
  TTL Serial JPEG Camera: TTL Serial JPEG Camera with NTSC Out
  1.8" TFT Display with uSD: 1.8" TFT Display with SPI control and MicroSD card
  1.8" TFT Display with uSD: 1.8" TFT Display with SPI control and MicroSD card
